// Logisim project BCD TO SEVEN SEGMENT DECODER LOGISIM LAB7.circ as structural Verilog: 1 circuit, main circuit main
module main (
  input  A,
  input  B,
  input  C,
  input  D
);

  wire and_1_out, and_2_out, and_3_out, and_4_out, and_5_out, and_6_out, and_7_out, and_8_out, and_9_out,
       and_10_out, and_11_out, and_12_out, and_13_out, and_14_out, and_15_out, and_16_out, not_1_out,
       not_2_out, not_3_out, not_4_out, not_5_out, not_6_out, not_7_out, not_8_out, not_9_out, not_10_out,
       not_11_out, not_12_out, not_13_out, not_14_out, not_15_out, not_16_out, not_17_out, not_18_out,
       or_1_out, or_2_out, or_3_out, or_4_out, or_5_out, or_6_out, or_7_out, or_8_out, or_9_out, or_10_out,
       or_11_out, or_12_out, or_13_out, or_14_out, or_15_out, or_16_out, or_17_out, or_18_out;

  not not_1 (not_1_out, B);
  not not_2 (not_2_out, D);
  not not_3 (not_3_out, B);
  and and_1 (and_1_out, not_3_out, not_4_out);
  not not_4 (not_4_out, D);
  not not_5 (not_5_out, C);
  and and_2 (and_2_out, not_5_out, D);
  not not_6 (not_6_out, B);
  not not_7 (not_7_out, C);
  and and_3 (and_3_out, not_7_out, not_8_out);
  not not_8 (not_8_out, D);
  not not_9 (not_9_out, C);
  not not_10 (not_10_out, B);
  not not_11 (not_11_out, C);
  not not_12 (not_12_out, C);
  not not_13 (not_13_out, C);
  and and_4 (and_4_out, not_13_out, D);
  and and_5 (and_5_out, B, D, C);
  not not_14 (not_14_out, B);
  not not_15 (not_15_out, C);
  not not_16 (not_16_out, D);
  or or_1 (or_1_out, and_1_out, and_2_out);
  and and_6 (and_6_out, C, not_6_out);
  and and_7 (and_7_out, B, D);
  and and_8 (and_8_out, not_11_out, not_12_out);
  and and_9 (and_9_out, C, D);
  not not_17 (not_17_out, B);
  and and_10 (and_10_out, not_17_out, not_18_out);
  not not_18 (not_18_out, D);
  and and_11 (and_11_out, B, C);
  and and_12 (and_12_out, not_14_out, C);
  and and_13 (and_13_out, not_1_out, not_2_out);
  or or_2 (or_2_out, and_6_out, and_3_out);
  or or_3 (or_3_out, not_10_out, and_8_out);
  or or_4 (or_4_out, and_10_out, and_11_out);
  or or_5 (or_5_out, and_4_out, and_5_out);
  and and_14 (and_14_out, not_15_out, B);
  or or_6 (or_6_out, or_2_out, and_7_out);
  or or_7 (or_7_out, or_3_out, and_9_out);
  or or_8 (or_8_out, or_4_out, A);
  or or_9 (or_9_out, and_12_out, and_14_out);
  or or_10 (or_10_out, and_13_out, C);
  and and_15 (and_15_out, B, D);
  or or_11 (or_11_out, or_6_out, A);
  or or_12 (or_12_out, or_8_out, or_5_out);
  and and_16 (and_16_out, not_16_out, B);
  or or_13 (or_13_out, or_9_out, and_16_out);
  or or_14 (or_14_out, and_15_out, A);
  or or_15 (or_15_out, or_10_out, or_14_out);
  or or_16 (or_16_out, not_9_out, D);
  or or_17 (or_17_out, or_13_out, A);
  or or_18 (or_18_out, B, or_16_out);
  _7_Segment_Display u_7_segment_display_1 (
    .g(or_17_out), .f(or_11_out), .a(or_15_out), .b(or_7_out), .e(or_1_out), .d(or_12_out), .c(or_18_out));  // open: dp

  // Notes on the sheet:
  //   e
  //   f
  //   d
  //   a
  //   c
  //   b
endmodule
