// Logisim project Lab 4 BCD to Excess-3 LOGISIM.circ as structural Verilog: 4 circuits, main circuit 7432
module main (
  input  W,
  input  X,
  input  Y,
  input  Z,
  output D,
  output C,
  output B,
  output A
);

  wire n7404_1_out_6, n7404_1_out_7, n7404_1_out_8, n7408_1_out_17, n7408_1_out_18, n7408_1_out_19,
       n7408_1_out_20, n7408_1_out_21, n7408_1_out_22, n7408_1_out_23;

  _7404 u_7404_1 (
    .in_1(Z), .in_2(Y), .in_3(X), .in_4(W), .out_5(D), .out_6(n7404_1_out_6), .out_7(n7404_1_out_7),
    .out_8(n7404_1_out_8));
  _7408 u_7408_1 (
    .in_1(Z), .in_2(Y), .in_3(D), .in_4(n7404_1_out_6), .in_5(D), .in_6(n7408_1_out_20),
    .in_7(n7404_1_out_6), .in_8(X), .in_9(Y), .in_10(n7404_1_out_7), .in_11(Z), .in_12(n7404_1_out_7),
    .in_13(Z), .in_14(X), .in_15(Y), .in_16(X), .out_17(n7408_1_out_17), .out_18(n7408_1_out_18),
    .out_19(n7408_1_out_19), .out_20(n7408_1_out_20), .out_21(n7408_1_out_21), .out_22(n7408_1_out_22),
    .out_23(n7408_1_out_23), .out_24(n7408_1_out_23));
  _7432 u_7432_1 (
    .in_1(n7408_1_out_17), .in_2(n7408_1_out_18), .in_5(n7408_1_out_19), .in_6(n7408_1_out_21),
    .in_8(n7408_1_out_22), .in_9(W), .in_10(n7408_1_out_23), .in_11(n7408_1_out_23), .out_13(C), .out_14(B),
    .out_15(A));  // open: in_3, in_4, in_7, out_12
endmodule

module _7404 (
  input  in_1,
  input  in_2,
  input  in_3,
  input  in_4,
  output out_5,
  output out_6,
  output out_7,
  output out_8
);

  not not_1 (out_5, in_1);
  not not_2 (out_6, in_2);
  not not_3 (out_7, in_3);
  not not_4 (out_8, in_4);
endmodule

module _7432 (
  input  in_1,
  input  in_2,
  input  in_3,
  input  in_4,
  input  in_5,
  input  in_6,
  input  in_7,
  input  in_8,
  input  in_9,
  input  in_10,
  input  in_11,
  output out_12,
  output out_13,
  output out_14,
  output out_15
);

  or or_1 (out_12, in_1, in_2, in_3);
  or or_2 (out_13, in_4, in_5, in_6);
  or or_3 (out_14, in_7, in_8, in_9);
  or or_4 (out_15, in_10, in_11);
endmodule

module _7408 (
  input  in_1,
  input  in_2,
  input  in_3,
  input  in_4,
  input  in_5,
  input  in_6,
  input  in_7,
  input  in_8,
  input  in_9,
  input  in_10,
  input  in_11,
  input  in_12,
  input  in_13,
  input  in_14,
  input  in_15,
  input  in_16,
  output out_17,
  output out_18,
  output out_19,
  output out_20,
  output out_21,
  output out_22,
  output out_23,
  output out_24
);

  and and_1 (out_17, in_1, in_3);
  and and_2 (out_19, in_5, in_7);
  and and_3 (out_21, in_9, in_11);
  and and_4 (out_23, in_13, in_15);
  and and_5 (out_18, in_2, in_4);
  and and_6 (out_20, in_6, in_8);
  and and_7 (out_22, in_10, in_12);
  and and_8 (out_24, in_14, in_16);
endmodule
