// Logisim project lab1.circ as structural Verilog: 1 circuit, main circuit main
module main (
);

  wire A_out, B_out, C_out, I1_out, I2_out, I3_out, not_1_out, not_2_out, or_1_out, or_2_out;

  Button A (.out(A_out));
  Button C (.out(C_out));
  Button B (.out(B_out));
  not not_1 (not_1_out, A_out);
  not not_2 (not_2_out, B_out);
  and I1 (I1_out, not_1_out, C_out);
  and I2 (I2_out, A_out, not_2_out);
  and I3 (I3_out, B_out, C_out);
  or or_1 (or_1_out, I1_out, I2_out);
  or or_2 (or_2_out, or_1_out, I3_out);
  LED F (.in(or_2_out));
endmodule
