// Logisim project lab2-1.circ as structural Verilog: 1 circuit, main circuit main
module main (
);

  wire _1_2_out, _1_out, _2_2_out, _2_out, _3_out, A_2_out, A_3_out, A_out, B_out, NOT_out;

  Button A (.out(A_out));
  Button B (.out(B_out));
  Button A_2 (.out(A_2_out));
  Button A_3 (.out(A_3_out));
  nor NOT (NOT_out, A_3_out, A_3_out);
  nor _1 (_1_out, A_out, A_out);
  nor _2 (_2_out, B_out, B_out);
  nor _1_2 (_1_2_out, A_2_out, A_2_out);
  LED NOT_using_NOR (.in(NOT_out));
  nor _3 (_3_out, _1_out, _2_out);
  nor _2_2 (_2_2_out, _1_2_out, _1_2_out);
  LED AND_using_NOR (.in(_3_out));
  LED OR_using_NOR (.in(_2_2_out));
endmodule
