// Logisim project lab2-3.circ as structural Verilog: 1 circuit, main circuit main
module main (
);

  wire _1_2_out, _1_out, _2_2_out, _2_out, _3_out, A_2_out, A_3_out, A_4_out, A_5_out, A_out, B_2_out,
       B_3_out, B_out, C_2_out, C_out, D_2_out, D_out, E_2_out, E_out, F_2_out, F_out, g_out, NOT_out;

  Button A (.out(A_out));
  Button B (.out(B_out));
  Button A_2 (.out(A_2_out));
  Button B_2 (.out(B_2_out));
  Button A_3 (.out(A_3_out));
  Button B_3 (.out(B_3_out));
  Button A_4 (.out(A_4_out));
  Button A_5 (.out(A_5_out));
  nor C (C_out, A_out, B_out);
  nor NOT (NOT_out, A_5_out, A_5_out);
  nor _1 (_1_out, A_3_out, A_3_out);
  nor _2 (_2_out, B_3_out, B_3_out);
  nor _1_2 (_1_2_out, A_4_out, A_4_out);
  nor C_2 (C_2_out, A_2_out, B_2_out);
  LED NOT_using_NOR (.in(NOT_out));
  nor D (D_out, A_out, C_out);
  nor E (E_out, C_out, B_out);
  nor D_2 (D_2_out, A_2_out, C_2_out);
  nor _3 (_3_out, _1_out, _2_out);
  nor _2_2 (_2_2_out, _1_2_out, _1_2_out);
  nor F (F_out, D_out, E_out);
  nor E_2 (E_2_out, C_2_out, B_2_out);
  LED AND_using_NOR (.in(_3_out));
  nor F_2 (F_2_out, D_2_out, E_2_out);
  LED OR_using_NOR (.in(_2_2_out));
  nor g (g_out, F_out, F_out);
  LED X_NOR_using_NOR (.in(F_2_out));
  LED XOR_using_NOR (.in(g_out));
endmodule
